# Fritzing sketch Robotito (saved by Fritzing 0.9.3b)

parts:
  Raspberry_Pi_1 = Raspberry Pi 3 [part_number=RPI-3-V1.2]
  Battery1 = 18650Battery
  Battery2 = 18650Battery
  Battery3 = 18650Battery
  Motor_2 = DC Motor with two-phase hall-encoder [part_number=VT-E-G25A-06-177E]
  Motor3 = DC Motor with two-phase hall-encoder [part_number=VT-E-G25A-06-177E]
  Motor1 = DC Motor with two-phase hall-encoder [part_number=VT-E-G25A-06-177E]
  Part1 = Adafruit DC+Stepper Motor HAT [part_number="Adafruit #2348"]
  Motor_0 = DC Motor with two-phase hall-encoder [part_number=VT-E-G25A-06-177E]
  Part2 = Adafruit VL53L0X Time of Flight Distance Sensor [part_number="Adafruit #3317"]
  Part3 = Adafruit VL53L0X Time of Flight Distance Sensor [part_number="Adafruit #3317"]
  Part4 = Adafruit VL53L0X Time of Flight Distance Sensor [part_number="Adafruit #3317"]
  Part5 = Adafruit VL53L0X Time of Flight Distance Sensor [part_number="Adafruit #3317"]
  Part6 = PowerBoost 500 Charger
  S1 = SPST Switch [package=switch-spst-smd-a]

nets:
  VIN: Raspberry_Pi_1.3v3, Raspberry_Pi_1.3V3, Part1.3.3V, Part2.VIN, Part3.VIN, Part4.VIN, Part5.VIN, S1.P
  N1: Raspberry_Pi_1.GPIO2, Part1.SDA, Part2.SDA, Part3.SDA, Part4.SDA, Part5.SDA
  N2: Raspberry_Pi_1.GPIO3, Part1.SCL, Part2.SCL, Part3.SCL, Part4.SCL, Part5.SCL
  N3: Raspberry_Pi_1.GIPO4, Part1.GPIO4, Motor_0.pin4
  GND: Raspberry_Pi_1.GND, Battery3.+, Motor_2.pin2, Motor_2.pin5, Motor3.pin2, Motor3.pin5, Motor1.pin2, Motor1.pin5, Part1.GND, Motor_0.pin2, Motor_0.pin5, Part2.GND, Part3.GND, Part4.GND, Part5.GND
  N4: Raspberry_Pi_1.GIPO17, Part1.GPIO17, Motor_0.pin3
  N5: Raspberry_Pi_1.GIPO27, Motor1.pin3, Part1.GPIO27
  N6: Raspberry_Pi_1.GIPO22, Motor_2.pin4, Part1.GPIO22
  N7: Raspberry_Pi_1.GIPO10, Part1.SPI_MOSI
  N8: Raspberry_Pi_1.GIPO9, Part1.SPI_MISO
  N9: Raspberry_Pi_1.GIPO11, Part1.SPI_SCLK
  N10: Raspberry_Pi_1.ID_SD, Part1.EEDATA
  N11: Raspberry_Pi_1.GIPO5, Part1.GPIO5
  N12: Raspberry_Pi_1.GIPO6, Part1.GPIO6
  N13: Raspberry_Pi_1.GIPO13, Part1.GPIO13
  N14: Raspberry_Pi_1.GIPO19, Part1.GPIO19, Part3.XSHUT
  N15: Raspberry_Pi_1.GIPO26, Part1.GPIO26
  N16: Raspberry_Pi_1.GIPO21, Part1.GPIO21, Part5.XSHUT
  N17: Raspberry_Pi_1.GIPO20, Part1.GPIO20, Part4.XSHUT
  N18: Raspberry_Pi_1.GIPO16, Part1.GPIO16, Part2.XSHUT
  N19: Raspberry_Pi_1.GIPO12, Part1.GPIO12
  N20: Raspberry_Pi_1.ID_SC, Part1.EECLK
  N21: Raspberry_Pi_1.GIPO7, Part1.SPI_CE1
  N22: Raspberry_Pi_1.GIPO8, Part1.SPI_CE0
  N23: Raspberry_Pi_1.GIPO25, Motor3.pin3, Part1.GPIO25
  N24: Raspberry_Pi_1.GIPO24, Motor3.pin4, Part1.GPIO24
  N25: Raspberry_Pi_1.GIPO23, Motor_2.pin3, Part1.GPIO23
  N26: Raspberry_Pi_1.GIPO18, Motor1.pin4, Part1.GPIO18
  N27: Raspberry_Pi_1.GIPO15, Part1.RXD
  N28: Raspberry_Pi_1.GIPO14, Part1.TXD
  N29: Raspberry_Pi_1.5V, Part1.5.0V
  N30: Battery1.+, Battery2.-
  N31: Battery1.-, Part6.VBAT_OUT
  N32: Battery2.+, Battery3.-
  N33: Motor_2.pin1, Part1.M4B
  N34: Motor_2.pin6, Part1.M4A
  N35: Motor3.pin1, Part1.M2B
  N36: Motor3.pin6, Part1.M2A
  N37: Motor1.pin1, Part1.M3A
  N38: Motor1.pin6, Part1.M3B
  N39: Part1.M1B, Motor_0.pin6
  N40: Part1.M1A, Motor_0.pin1
  N41: Part1.VMOTOR, Part6.5.0V
  N42: Part6.ENABLE, S1.S
  N43: Part6.GND, S1.O

custom parts:
  18650Battery: 18650 Battery
  Adafruit DC+Stepper Motor HAT: Let your robotic dreams come true with the new DC+Stepper Motor HAT from Adafruit. This Raspberry Pi add-on is perfect for any motion project as it can drive up to 4 DC or 2 Stepper motors with full PWM speed control. Since the Raspberry Pi does not have a lot of PWM pins, we use a fully-dedicated PWM driver chip onboard to both control motor direction and speed. This chip handles all the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
  Adafruit VL53L0X Time of Flight Distance Sensor: The VL53L0X is a Time of Flight distance sensor like no other you've used! The sensor contains a very tiny invisible laser source, and a matching sensor. The VL53L0X can detect the "time of flight", or how long the light has taken to bounce back to the sensor. Since it uses a very narrow light source, it is good for determining distance of only the surface directly in front of it. Unlike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
